# Fritzing sketch 2023-0403-cds-1 (saved by Fritzing 0.8.7b)
breadboards: 1

parts:
  부품1 = Arduino Uno (Rev3)
  R1 = Photocell (LDR) [package=THT]
  R2 = Resistor [tolerance=±5% resistance=10k package=THT]

nets:
  N1: 부품1.A0, R1.pin_1, R2.Pin_0
  N2: 부품1.5V, R1.pin_0
  N3: 부품1.GND, R2.Pin_1
