# Fritzing sketch 2023-0410-dht-1 (saved by Fritzing 0.8.7b)
breadboards: 1

parts:
  부품1 = Arduino Uno (Rev3)
  Mod1 = KY-015 Temperature & Humidity Sensor Module [package="Breakout board"]

nets:
  N1: 부품1.GND, Mod1.-
  N2: 부품1.D2, Mod1.Vin
  N3: 부품1.5V, Mod1.S

custom parts:
  KY-015 Temperature & Humidity Sensor Module: KY-015 temperature and humidity sensor module, provides a low-latency serial interface to measure humidity and temperature.
