# Fritzing sketch 2023-0417-lcd-1 (saved by Fritzing 0.8.7b)
breadboards: 1

parts:
  부품1 = LCD1602-I2C
  부품2 = Arduino Uno (Rev3)

nets:
  GND: 부품1.GND, 부품2.GND
  VCC: 부품1.VCC, 부품2.5V
  N1: 부품1.SDA, 부품2.A4/SDA
  N2: 부품1.SCL, 부품2.A5/SCL

custom parts:
  LCD1602-I2C: A standard character display, usually with 2x16 characters. Comes in many colors with LCM1602 IIC attached.
