# Fritzing sketch 2023-0327-led-1 (saved by Fritzing 0.8.7b)
breadboards: 1

parts:
  부품1 = Arduino Uno (Rev3)
  R1 = Resistor [tolerance=±5% resistance=330 package=THT]
  LED1 = LED - 5mm [color="Red (633nm)" package="5 mm [THT]"]

nets:
  N1: 부품1.D13/SCK, LED1.anode
  N2: 부품1.GND, R1.Pin_1
  N3: R1.Pin_0, LED1.cathode
