# Fritzing sketch mission_1 (saved by Fritzing 0.8.7b)
breadboards: 1

parts:
  부품1 = LCD1602-I2C
  부품2 = Arduino Uno (Rev3)
  R1 = Resistor [tolerance=±5% resistance=220 package=THT]
  R2 = PHOTOCELL [package=photocell-kit]
  Mod1 = KY-015 Temperature & Humidity Sensor Module [package="Breakout board"]

nets:
  GND: 부품1.GND, 부품2.GND, R1.Pin_1, Mod1.-
  VCC: 부품1.VCC, 부품2.5V, R2.P$1, Mod1.Vin
  N1: 부품1.SDA, 부품2.A4/SDA
  N2: 부품1.SCL, 부품2.A5/SCL
  N3: 부품2.A0, R1.Pin_0, R2.P$2
  N4: 부품2.D5_PWM, Mod1.S

custom parts:
  LCD1602-I2C: A standard character display, usually with 2x16 characters. Comes in many colors with LCM1602 IIC attached.
  KY-015 Temperature & Humidity Sensor Module: KY-015 temperature and humidity sensor module, provides a low-latency serial interface to measure humidity and temperature.
